# Fritzing sketch Rubix Cube Solver (saved by Fritzing 1.0.0rc)
circuit board: 8.46667cm x 5.64444cm

parts:
  2N2222 = NPN-Transistor [package="TO92 [THT]"]
  2N2222_2 = NPN-Transistor [package="TO92 [THT]"]
  R1 = Resistor [tolerance=±5% power=0.25W resistance=1k package=THT]
  R2 = Resistor [tolerance=±5% power=0.25W resistance=1k package=THT]
  2N2222_3 = NPN-Transistor [package="TO92 [THT]"]
  R3 = Resistor [tolerance=±5% power=0.25W resistance=1k package=THT]
  LED1 = RGB LED (com. cathode, rgb) [color="Red (633nm)" current=0.030A package="5 mm [THT]"]
  LED2 = RGB LED (com. cathode, rgb) [color="Red (633nm)" current=0.030A package="5 mm [THT]"]
  LED3 = RGB LED (com. cathode, rgb) [color="Red (633nm)" current=0.030A package="5 mm [THT]"]
  LED4 = RGB LED (com. cathode, rgb) [color="Red (633nm)" current=0.030A package="5 mm [THT]"]
  LED5 = RGB LED (com. cathode, rgb) [color="Red (633nm)" current=0.030A package="5 mm [THT]"]
  LED6 = RGB LED (com. cathode, rgb) [color="Red (633nm)" current=0.030A package="5 mm [THT]"]
  LED7 = RGB LED (com. cathode, rgb) [color="Red (633nm)" current=0.030A package="5 mm [THT]"]
  LED8 = RGB LED (com. cathode, rgb) [color="Red (633nm)" current=0.030A package="5 mm [THT]"]
  LED9 = RGB LED (com. cathode, rgb) [color="Red (633nm)" current=0.030A package="5 mm [THT]"]
  LED10 = RGB LED (com. cathode, rgb) [color="Red (633nm)" current=0.030A package="5 mm [THT]"]
  R4 = Resistor [tolerance=±5% power=0.25W resistance=470 package=THT]
  R5 = Resistor [tolerance=±5% power=0.25W resistance=470 package=THT]
  R6 = Resistor [tolerance=±5% power=0.25W resistance=470 package=THT]
  R7 = Resistor [tolerance=±5% power=0.25W resistance=470 package=THT]
  R8 = Resistor [tolerance=±5% power=0.25W resistance=470 package=THT]
  R9 = Resistor [tolerance=±5% power=0.25W resistance=470 package=THT]
  R10 = Resistor [tolerance=±5% power=0.25W resistance=470 package=THT]
  R11 = Resistor [tolerance=±5% power=0.25W resistance=470 package=THT]
  R12 = Resistor [tolerance=±5% power=0.25W resistance=470 package=THT]
  R13 = Resistor [tolerance=±5% power=0.25W resistance=470 package=THT]
  R14 = Resistor [tolerance=±5% power=0.25W resistance=430 package=THT]
  R16 = Resistor [tolerance=±5% power=0.25W resistance=430 package=THT]
  R17 = Resistor [tolerance=±5% power=0.25W resistance=430 package=THT]
  R18 = Resistor [tolerance=±5% power=0.25W resistance=430 package=THT]
  R19 = Resistor [tolerance=±5% power=0.25W resistance=430 package=THT]
  R20 = Resistor [tolerance=±5% power=0.25W resistance=430 package=THT]
  R21 = Resistor [tolerance=±5% power=0.25W resistance=430 package=THT]
  R22 = Resistor [tolerance=±5% power=0.25W resistance=430 package=THT]
  R23 = Resistor [tolerance=±5% power=0.25W resistance=430 package=THT]
  R15 = Resistor [tolerance=±5% power=0.25W resistance=430 package=THT]
  R24 = Resistor [tolerance=±5% power=0.25W resistance=430 package=THT]
  R25 = Resistor [tolerance=±5% power=0.25W resistance=430 package=THT]
  R26 = Resistor [tolerance=±5% power=0.25W resistance=430 package=THT]
  R27 = Resistor [tolerance=±5% power=0.25W resistance=430 package=THT]
  R28 = Resistor [tolerance=±5% power=0.25W resistance=430 package=THT]
  R29 = Resistor [tolerance=±5% power=0.25W resistance=430 package=THT]
  R30 = Resistor [tolerance=±5% power=0.25W resistance=430 package=THT]
  R31 = Resistor [tolerance=±5% power=0.25W resistance=430 package=THT]
  R32 = Resistor [tolerance=±5% power=0.25W resistance=430 package=THT]
  R33 = Resistor [tolerance=±5% power=0.25W resistance=430 package=THT]
  Teensy1 = Teensy 4.1
  PT_1 = LTR-301 [package=ltr-301]
  R34 = Resistor [tolerance=±5% power=0.25W resistance=100k package=THT]
  PT_2 = LTR-301 [package=ltr-301]
  R35 = Resistor [tolerance=±5% power=0.25W resistance=100k package=THT]
  PT_3 = LTR-301 [package=ltr-301]
  R36 = Resistor [tolerance=±5% power=0.25W resistance=100k package=THT]
  PT_4 = LTR-301 [package=ltr-301]
  PT_6 = LTR-301 [package=ltr-301]
  PT_5 = LTR-301 [package=ltr-301]
  R37 = Resistor [tolerance=±5% power=0.25W resistance=100k package=THT]
  R38 = Resistor [tolerance=±5% power=0.25W resistance=100k package=THT]
  R39 = Resistor [tolerance=±5% power=0.25W resistance=100k package=THT]
  PT_7 = LTR-301 [package=ltr-301]
  PT_9 = LTR-301 [package=ltr-301]
  PT_8 = LTR-301 [package=ltr-301]
  R40 = Resistor [tolerance=±5% power=0.25W resistance=100k package=THT]
  R41 = Resistor [tolerance=±5% power=0.25W resistance=100k package=THT]
  R42 = Resistor [tolerance=±5% power=0.25W resistance=100k package=THT]
  PT_10 = LTR-301 [package=ltr-301]
  R43 = Resistor [tolerance=±5% power=0.25W resistance=100k package=THT]
  12V_Regulator = RioRand LM2596
  DC_Power_Supply = DC Power [voltage=24]
  On_Switch = Pushbutton [package=THT]
  5V_Regulator = RioRand LM2596
  Top_Servo = Basic Servo
  Bottom_Servo = Basic Servo
  Cooling_Fan = Fan - Ventilador [package=THT]
  LED11 = RGB LED (com. cathode, rgb) [color="Red (633nm)" current=0.030A package="5 mm [THT]"]
  R44 = Resistor [tolerance=±5% power=0.25W resistance=220 package=THT]
  R45 = Resistor [tolerance=±5% power=0.25W resistance=220 package=THT]
  R46 = Resistor [tolerance=±5% power=0.25W resistance=330 package=THT]
  LED12 = RGB LED (com. cathode, rgb) [color="Red (633nm)" current=0.030A package="5 mm [THT]"]
  R47 = Resistor [tolerance=±5% power=0.25W resistance=330 package=THT]
  R48 = Resistor [tolerance=±5% power=0.25W resistance=220 package=THT]
  R49 = Resistor [tolerance=±5% power=0.25W resistance=220 package=THT]
  PT_11 = LTR-301 [package=ltr-301]
  R50 = Resistor [tolerance=±5% power=0.25W resistance=100k package=THT]
  PT_12 = LTR-301 [package=ltr-301]
  R51 = Resistor [tolerance=±5% power=0.25W resistance=100k package=THT]
  Button_1 = Momentary Switch [package=ksa_sealed_tac_switch]
  Button_2 = Momentary Switch [package=ksa_sealed_tac_switch]
  R52 = Resistor [tolerance=±5% power=0.25W resistance=1k package=THT]
  R53 = Resistor [tolerance=±5% power=0.25W resistance=1k package=THT]
  SSD1306_I2C_Display = Grove OLED 128x96
  M1_Driver = IC, DIP package, 16 pins [chip_label=TMC2208]
  M1 = Stepper Motor - Bipolar
  M2_Driver = IC, DIP package, 16 pins [chip_label=TMC2208]
  M2 = Stepper Motor - Bipolar
  M4_Driver = IC, DIP package, 16 pins [chip_label=TMC2208]
  M3_Driver = IC, DIP package, 16 pins [chip_label=TMC2208]
  M3 = Stepper Motor - Bipolar
  M4 = Stepper Motor - Bipolar
  M6_Driver = IC, DIP package, 16 pins [chip_label=TMC2208]
  M5_Driver = IC, DIP package, 16 pins [chip_label=TMC2208]
  M5 = Stepper Motor - Bipolar
  M6 = Stepper Motor - Bipolar
  M7_Driver = IC, DIP package, 16 pins [chip_label=TMC2208]
  M7_(Slide_Track) = Stepper Motor - Bipolar
  Power_LED = LED - 5mm [color="Red (633nm)" current=0.030A package="5 mm [THT]"]
  R54 = Resistor [tolerance=±5% power=0.25W resistance=470 package=THT]
  C2 = Electrolytic Capacitor [capacitance=0.1mF voltage=35V package="100 mil [THT, electrolytic]"]
  C1 = Electrolytic Capacitor [capacitance=0.1mF voltage=35V package="100 mil [THT, electrolytic]"]
  C3 = Electrolytic Capacitor [capacitance=0.1mF voltage=35V package="100 mil [THT, electrolytic]"]
  C4 = Electrolytic Capacitor [capacitance=0.1mF voltage=35V package="100 mil [THT, electrolytic]"]
  C5 = Electrolytic Capacitor [capacitance=0.1mF voltage=35V package="100 mil [THT, electrolytic]"]
  C6 = Electrolytic Capacitor [capacitance=0.1mF voltage=35V package="100 mil [THT, electrolytic]"]
  C7 = Electrolytic Capacitor [capacitance=0.1mF voltage=35V package="100 mil [THT, electrolytic]"]

nets:
  N1: 2N2222.E, R24.Pin_1, R25.Pin_1, R26.Pin_1, R27.Pin_1, R28.Pin_1, R29.Pin_1, R30.Pin_1, R31.Pin_1, R32.Pin_1, R33.Pin_1
  N2: 2N2222.B, R1.Pin_1
  N3: 2N2222.C, 2N2222_2.C, 2N2222_3.C, 12V_Regulator.Pin_3, Cooling_Fan.5V, Power_LED.anode
  N4: 2N2222_2.E, R14.Pin_1, R16.Pin_1, R17.Pin_1, R18.Pin_1, R19.Pin_1, R20.Pin_1, R21.Pin_1, R22.Pin_1, R23.Pin_1, R15.Pin_1
  N5: 2N2222_2.B, R2.Pin_1
  N6: R1.Pin_0, Teensy1.A15/D39
  N7: R2.Pin_0, Teensy1.A16/D40
  N8: 2N2222_3.E, R4.Pin_1, R5.Pin_1, R6.Pin_1, R7.Pin_1, R8.Pin_1, R9.Pin_1, R10.Pin_1, R11.Pin_1, R12.Pin_1, R13.Pin_1
  N9: 2N2222_3.B, R3.Pin_1
  N10: R3.Pin_0, Teensy1.A17/D41
  N11: LED1.red_anode, R4.Pin_0
  GND: LED1.common_cathode, LED2.common_cathode, LED3.common_cathode, LED4.common_cathode, LED5.common_cathode, LED6.common_cathode, LED7.common_cathode, LED8.common_cathode, LED9.common_cathode, LED10.common_cathode, Teensy1.GND2, R34.Pin_0, R35.Pin_0, R36.Pin_0, R37.Pin_0, R38.Pin_0, R39.Pin_0, R40.Pin_0, R41.Pin_0, R42.Pin_0, R43.Pin_0, 12V_Regulator.Pin_2, 12V_Regulator.Pin_4, DC_Power_Supply.V-, 5V_Regulator.Pin_2, 5V_Regulator.Pin_4, Top_Servo.gnd, Bottom_Servo.gnd, Cooling_Fan.GND, LED11.common_cathode, LED12.common_cathode, R50.Pin_0, R51.Pin_0, R52.Pin_0, R53.Pin_0, SSD1306_I2C_Display.GND, M1_Driver.pin1, M1_Driver.pin7, M2_Driver.pin7, M4_Driver.pin7, M3_Driver.pin7, M6_Driver.pin7, M5_Driver.pin7, M7_Driver.pin7, R54.Pin_0, C2.-, C1.-, C3.-, C4.-, C5.-, C6.-, C7.-
  N12: LED1.green_anode, R14.Pin_0
  N13: LED1.blue_anode, R24.Pin_0
  N14: LED2.red_anode, R5.Pin_0
  N15: LED2.green_anode, R15.Pin_0
  N16: LED2.blue_anode, R25.Pin_0
  N17: LED3.red_anode, R6.Pin_0
  N18: LED3.green_anode, R16.Pin_0
  N19: LED3.blue_anode, R26.Pin_0
  N20: LED4.red_anode, R7.Pin_0
  N21: LED4.green_anode, R17.Pin_0
  N22: LED4.blue_anode, R27.Pin_0
  N23: LED5.red_anode, R8.Pin_0
  N24: LED5.green_anode, R18.Pin_0
  N25: LED5.blue_anode, R28.Pin_0
  N26: LED6.red_anode, R9.Pin_0
  N27: LED6.green_anode, R19.Pin_0
  N28: LED6.blue_anode, R29.Pin_0
  N29: LED7.red_anode, R10.Pin_0
  N30: LED7.green_anode, R20.Pin_0
  N31: LED7.blue_anode, R30.Pin_0
  N32: LED8.red_anode, R11.Pin_0
  N33: LED8.green_anode, R21.Pin_0
  N34: LED8.blue_anode, R31.Pin_0
  N35: LED9.red_anode, R12.Pin_0
  N36: LED9.green_anode, R22.Pin_0
  N37: LED9.blue_anode, R32.Pin_0
  N38: LED10.red_anode, R13.Pin_0
  N39: LED10.green_anode, R23.Pin_0
  N40: LED10.blue_anode, R33.Pin_0
  N41: Teensy1.D0, M1_Driver.pin9, M2_Driver.pin9, M4_Driver.pin9, M3_Driver.pin9, M6_Driver.pin9, M5_Driver.pin9, M7_Driver.pin9
  N42: Teensy1.D1, M1_Driver.pin16
  N43: Teensy1.D2, M1_Driver.pin15
  N44: Teensy1.D3, M2_Driver.pin16
  N45: Teensy1.D4, M2_Driver.pin15
  N46: Teensy1.D5, M3_Driver.pin16
  N47: Teensy1.D6, M3_Driver.pin15
  N48: Teensy1.D7, M4_Driver.pin16
  N49: Teensy1.D8, M4_Driver.pin15
  N50: Teensy1.D9, M5_Driver.pin16
  N51: Teensy1.D10, M5_Driver.pin15
  N52: Teensy1.D11, M6_Driver.pin16
  N53: Teensy1.D12, M6_Driver.pin15
  N54: Teensy1.A0/D14, PT_10.E, R43.Pin_1
  N55: Teensy1.A1/D15, PT_9.E, R42.Pin_1
  N56: Teensy1.A2/D16, PT_8.E, R40.Pin_1
  N57: Teensy1.A3/D17, PT_7.E, R41.Pin_1
  N58: Teensy1.A4/D18, PT_6.E, R39.Pin_1
  N59: Teensy1.A5/D19, PT_5.E, R37.Pin_1
  N60: Teensy1.A6/D20, PT_4.E, R38.Pin_1
  N61: Teensy1.A7/D21, PT_3.E, R36.Pin_1
  N62: Teensy1.A8/D22, PT_2.E, R35.Pin_1
  N63: Teensy1.A9/D23, PT_1.E, R34.Pin_1
  N64: Teensy1.3V3_LOW, PT_1.C, PT_2.C, PT_3.C, PT_4.C, PT_6.C, PT_5.C, PT_7.C, PT_9.C, PT_8.C, PT_10.C, PT_11.C, PT_12.C, Button_1.3, Button_2.4, SSD1306_I2C_Display.VCC, M1_Driver.pin2, M1_Driver.pin10, M2_Driver.pin2, M2_Driver.pin10, M4_Driver.pin2, M4_Driver.pin10, M3_Driver.pin2, M3_Driver.pin10, M6_Driver.pin2, M6_Driver.pin10, M5_Driver.pin2, M5_Driver.pin10, M7_Driver.pin2, M7_Driver.pin10
  VCC: Teensy1.Vin, 5V_Regulator.Pin_3, Top_Servo.vcc, Bottom_Servo.vcc
  N65: Teensy1.A10/D24, SSD1306_I2C_Display.SDA
  N66: Teensy1.A11/D25, SSD1306_I2C_Display.SCL
  N67: Teensy1.A12/D26, PT_11.E, R50.Pin_1
  N68: Teensy1.A13/D27, PT_12.E, R51.Pin_1
  N69: Teensy1.D28, M7_Driver.pin16
  N70: Teensy1.D29, M7_Driver.pin15
  N71: Teensy1.D31, Button_1.1
  N72: Teensy1.D32, Button_2.1
  N73: Teensy1.D33, R44.Pin_1, R49.Pin_1
  N74: Teensy1.D34, R45.Pin_1, R48.Pin_1
  N75: Teensy1.D35, R46.Pin_1, R47.Pin_1
  N76: Teensy1.D36, Bottom_Servo.pulse
  N77: Teensy1.D37, Top_Servo.pulse
  N78: 12V_Regulator.Pin_1, On_Switch.leg1, 5V_Regulator.Pin_1, M1_Driver.pin8, M2_Driver.pin8, M4_Driver.pin8, M3_Driver.pin8, M6_Driver.pin8, M5_Driver.pin8, M7_Driver.pin8, C2.+, C1.+, C3.+, C4.+, C5.+, C6.+, C7.+
  N79: DC_Power_Supply.V+, On_Switch.leg0
  N80: LED11.red_anode, R46.Pin_0
  N81: LED11.green_anode, R45.Pin_0
  N82: LED11.blue_anode, R44.Pin_0
  N83: LED12.red_anode, R47.Pin_0
  N84: LED12.green_anode, R48.Pin_0
  N85: LED12.blue_anode, R49.Pin_0
  N86: Button_1.2, R53.Pin_1
  N87: Button_2.2, R52.Pin_1
  N88: M1_Driver.pin3, M1.B
  N89: M1_Driver.pin4, M1.D
  N90: M1_Driver.pin5, M1.C
  N91: M1_Driver.pin6, M1.A
  N92: M2_Driver.pin3, M2.B
  N93: M2_Driver.pin4, M2.D
  N94: M2_Driver.pin5, M2.C
  N95: M2_Driver.pin6, M2.A
  N96: M4_Driver.pin3, M4.B
  N97: M4_Driver.pin4, M4.D
  N98: M4_Driver.pin5, M4.C
  N99: M4_Driver.pin6, M4.A
  N100: M3_Driver.pin3, M3.B
  N101: M3_Driver.pin4, M3.D
  N102: M3_Driver.pin5, M3.C
  N103: M3_Driver.pin6, M3.A
  N104: M6_Driver.pin3, M6.B
  N105: M6_Driver.pin4, M6.D
  N106: M6_Driver.pin5, M6.C
  N107: M6_Driver.pin6, M6.A
  N108: M5_Driver.pin3, M5.B
  N109: M5_Driver.pin4, M5.D
  N110: M5_Driver.pin5, M5.C
  N111: M5_Driver.pin6, M5.A
  N112: M7_Driver.pin3, M7_(Slide_Track).B
  N113: M7_Driver.pin4, M7_(Slide_Track).D
  N114: M7_Driver.pin5, M7_(Slide_Track).C
  N115: M7_Driver.pin6, M7_(Slide_Track).A
  N116: Power_LED.cathode, R54.Pin_1

notes:
  Color Sensor Phototransistors
  Color Sensor RGB LEDs
  Orientation LEDs
  Orientation Phototransistors

custom parts:
  Teensy 4.1: The Teensy is a complete USB-based microcontoller development system, in a very small footprint, capable of implementing many types of projects. All programming is done via the USB port. No special programmer is needed, only a standard micro-USB cable and a PC or Macintosh with a USB port.
  Fan - Ventilador: Ventilador de 2 pines, se encuentra comunmente en computadoras de escritorio
